# Fritzing sketch JukeBox (saved by Fritzing 1.0.6)
breadboards: 1

parts:
  U3 = 74HC595 [package="DIP16 [THT]"]
  R3 = Resistor [tolerance=±5% resistance=220 package="0402 [SMD]"]
  R4 = Resistor [tolerance=±5% resistance=220 package="0402 [SMD]"]
  R5 = Resistor [tolerance=±5% resistance=220 package="0402 [SMD]"]
  R6 = Resistor [tolerance=±5% resistance=220 package="0402 [SMD]"]
  R7 = Resistor [tolerance=±5% resistance=220 package="0402 [SMD]"]
  R8 = Resistor [tolerance=±5% resistance=220 package="0402 [SMD]"]
  R9 = Resistor [tolerance=±5% resistance=220 package="0402 [SMD]"]
  R10 = Resistor [tolerance=±5% resistance=220 package="0402 [SMD]"]
  U2 = TRANSISTOR_NPN_2 [package=to-92]
  R11 = Resistor [tolerance=±5% resistance=220 package="0402 [SMD]"]
  Part1 = LCD1602-I2C
  R12 = Rotary Potentiometer (Large) [maximum_resistance=10kΩ knob_status=50% power=0.5W package=THT]
  D2 = LED GRAPH [package=led_bargaph_10]
  SG1 = Buzzer 12mm [part_number=COM-07950 package=buzzer-12mm-ns]
  Part2 = Freenove ESP32 S3 GPIO Extension
  S2 = Pushbutton [package="[THT]"]

nets:
  N1: U3.Q1, D2.I_A
  N2: U3.Q2, D2.H_A
  N3: U3.Q3, D2.G_A
  N4: U3.Q4, D2.F_A
  N5: U3.Q5, D2.E_A
  N6: U3.Q6, D2.D_A
  N7: U3.Q7, D2.C_A
  GND: U3.GND, U3.OE, R3.Pin_0, R4.Pin_0, R5.Pin_0, R6.Pin_0, R7.Pin_0, R8.Pin_0, R9.Pin_0, R10.Pin_0, U2.C, Part1.GND, R12.leg1, Part2.pin_43, Part2.pin_44, S2.Pin_1, S2.Pin_2
  5V: U3.MR, U3.VCC, Part1.VCC, R12.leg2, SG1.1, Part2.pin_41#41, Part2.pin_42#42
  N8: U3.SH_CP, Part2.pin_14, Part2.5V
  N9: U3.ST_CP, Part2.pin_13
  N10: U3.DS, Part2.pin_12
  N11: U3.Q0, D2.J_A
  N12: R3.Pin_1, D2.I_C
  N13: R4.Pin_1, D2.H_C
  N14: R5.Pin_1, D2.G_C
  N15: R6.Pin_1, D2.F_C
  N16: R7.Pin_1, D2.E_C
  N17: R8.Pin_1, D2.D_C
  N18: R9.Pin_1, D2.C_C
  N19: R10.Pin_1, D2.J_C
  N20: U2.B, R11.Pin_1
  N21: U2.E, SG1.2
  N22: R11.Pin_0, Part2.pin_10
  N23: Part1.SDA, Part2.pin_18
  N24: Part1.SCL, Part2.pin_8
  N25: R12.wiper, Part2.pin_4
  N26: Part2.pin_9, Part2.GND, Part2.pin_35, Part2.pin_36, Part2.pin_40, Part2.TX
  N27: Part2.pin_48, S2.Pin_3, S2.Pin_4

custom parts:
  LCD1602-I2C: A standard character display, usually with 2x16 characters. Comes in many colors with LCM1602 IIC attached.
  LED GRAPH: 10-Segment LED Bar Graph SFE part numbers: COM-09935 (red, Vf = 2.1V, Ifmax = 20mA) COM-09936 (yellow, Vf = 2.1V, Ifmax = 20mA) COM-09937 (blue, Vf = 3.4V, Ifmax = 20mA) COM-09938 (green, Vf = 3.4V, Ifmax = 20mA)
  Buzzer 12mm: Buzzer 12mm Spark Fun Electronics SKU : Comp-Buzzer Through hole This is a small 12mm round speaker that operates around the audible 2kHz range. You can use these speakers to create simple music or user interfaces. This is not a true piezoelectric speaker but behaves similarly. Instead of a piezoelectric crystal that vibrates with an electric current, this tiny speaker uses an electromagnet to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
